// Logisim project exercicios-portas.circ as structural Verilog: 1 circuit, main circuit main
module main (
  input  A,
  input  A_2,
  input  B,
  input  B_2,
  input  C,
  input  C_2,
  input  D,
  input  A_3,
  input  A_4,
  input  B_3,
  input  B_4,
  input  C_3,
  input  C_4,
  input  D_2,
  input  D_3,
  input  A_5,
  input  A_6,
  input  B_5,
  input  B_6,
  input  C_5,
  input  C_6,
  input  D_4,
  input  D_5,
  input  E,
  input  A_7,
  input  in_26,
  input  B_7,
  input  in_28,
  input  C_7,
  input  in_30,
  input  D_6,
  input  A_8,
  input  A_9,
  input  B_8,
  input  B_9,
  input  C_8,
  input  C_9,
  input  D_7,
  input  D_8,
  output S,
  output S_2,
  output S_3,
  output S_4,
  output S_5,
  output S_6,
  output out_46,
  output S_7,
  output out_48,
  output out_49
);

  wire and_1_out, and_2_out, and_3_out, and_4_out, and_5_out, and_6_out, and_7_out, and_8_out, and_9_out,
       and_10_out, and_11_out, and_12_out, and_13_out, and_14_out, and_15_out, and_16_out, and_17_out,
       nand_1_out, nand_3_out, nand_4_out, not_1_out, not_2_out, not_3_out, not_4_out, not_5_out, not_6_out,
       not_7_out, not_8_out, or_1_out, or_4_out, or_5_out, or_7_out, or_8_out, or_10_out, xnor_1_out;

  and and_1 (and_1_out, A, B);
  not not_1 (not_1_out, B_3);
  nand nand_1 (nand_1_out, C_3, D_2);
  and and_2 (and_2_out, A_5, B_5);
  and and_3 (and_3_out, C_5, D_4);
  or or_1 (or_1_out, A_7, C_7);
  not not_2 (not_2_out, D_6);
  and and_4 (and_4_out, A_8, not_3_out);
  not not_3 (not_3_out, B_8);
  not not_4 (not_4_out, C_8);
  and and_5 (and_5_out, not_4_out, D_7);
  nand nand_2 (S_2, and_1_out, C);
  and and_6 (and_6_out, A_3, not_1_out);
  nor nor_1 (S_3, and_6_out, nand_1_out);
  or or_2 (S_6, and_2_out, and_7_out);
  and and_7 (and_7_out, and_3_out, E);
  and and_8 (and_8_out, B_7, not_2_out);
  or or_3 (out_48, and_4_out, and_5_out);
  xor xor_1 (S_7, or_1_out, and_8_out);
  not not_5 (not_5_out, A_2);
  and and_9 (and_9_out, C_2, D);
  or or_4 (or_4_out, B_2, and_9_out);
  and and_10 (and_10_out, A_4, B_4);
  not not_6 (not_6_out, C_4);
  or or_5 (or_5_out, A_6, B_6);
  and and_11 (and_11_out, C_6, D_5);
  not not_7 (not_7_out, in_28);
  not not_8 (not_8_out, in_30);
  and and_12 (and_12_out, A_9, B_9);
  or or_6 (S, not_5_out, or_4_out);
  and and_13 (and_13_out, and_10_out, not_6_out);
  nand nand_3 (nand_3_out, C_4, D_3);
  and and_14 (and_14_out, or_5_out, or_7_out);
  or or_7 (or_7_out, B_6, and_11_out);
  xnor xnor_1 (xnor_1_out, in_26, not_7_out);
  and and_15 (and_15_out, and_12_out, D_8);
  or or_8 (or_8_out, and_13_out, nand_3_out);
  or or_9 (S_5, A_6, and_14_out);
  xor xor_2 (out_46, xnor_1_out, not_8_out);
  and and_16 (and_16_out, C_9, B_9);
  xnor xnor_2 (S_4, or_8_out, D_3);
  and and_17 (and_17_out, and_16_out, A_9);
  or or_10 (or_10_out, and_15_out, and_17_out);
  xor xor_3 (out_49, or_10_out, nand_4_out);
  nand nand_4 (nand_4_out, A_9, C_9);
endmodule
